// Logisim project P5（含转发）.circ as structural Verilog: 20 circuits, main circuit main
module GRF (
  input  clk,
  input  reset,
  input  we,
  input  [4:0] a1,
  input  [4:0] a2,
  input  [31:0] wd,
  input  [4:0] a3,
  output [31:0] rd1,
  output [31:0] rd2
);

  wire and_1_out, and_2_out, comparator_1_eq, comparator_2_eq, comparator_3_eq, comparator_4_eq, not_1_out,
       not_2_out;
  wire [31:0] I00, I01, I02, I03, I04, I05, I06, I07, I10, I11, I12, I13, I14, I15, I16, I17, I20, I21, I22,
       I23, I24, I25, I26, I27, I30, I31, I32, I33, I34, I35, I36, I37, multiplexer_1_out, multiplexer_2_out,
       O01, O02, O03, O04, O05, O06, O07, O10, O11, O12, O13, O14, O15, O16, O17, O20, O21, O22, O23, O24,
       O25, O26, O27, O30, O31, O32, O33, O34, O35, O36, O37;

  Demultiplexer #(.select(5), .width(32), .tristate("true")) demultiplexer_1 (
    .out0(I00), .out1(I01), .out2(I02), .out3(I03), .out4(I04), .out5(I05), .out6(I06), .out7(I07),
    .out8(I10), .out9(I11), .out10(I12), .out11(I13), .out12(I14), .out13(I15), .out14(I16), .out15(I17),
    .out16(I20), .out17(I21), .out18(I22), .out19(I23), .out20(I24), .out21(I25), .out22(I26), .out23(I27),
    .out24(I30), .out25(I31), .out26(I32), .out27(I33), .out28(I34), .out29(I35), .out30(I36), .out31(I37),
    .in(wd), .sel(a3));  // open: en
  Register #(.width(32)) register_1 (.D(I01), .en(we), .Q(O01), .clk(clk), .clr(reset));
  Register #(.width(32)) register_2 (.D(I02), .en(we), .Q(O02), .clk(clk), .clr(reset));
  Register #(.width(32)) register_3 (.D(I03), .en(we), .Q(O03), .clk(clk), .clr(reset));
  Register #(.width(32)) register_4 (.D(I04), .en(we), .Q(O04), .clk(clk), .clr(reset));
  Register #(.width(32)) register_5 (.D(I05), .en(we), .Q(O05), .clk(clk), .clr(reset));
  Register #(.width(32)) register_6 (.D(I06), .en(we), .Q(O06), .clk(clk), .clr(reset));
  Register #(.width(32)) register_7 (.D(I07), .en(we), .Q(O07), .clk(clk), .clr(reset));
  Register #(.width(32)) register_8 (.D(I10), .en(we), .Q(O10), .clk(clk), .clr(reset));
  Register #(.width(32)) register_9 (.D(I11), .en(we), .Q(O11), .clk(clk), .clr(reset));
  Register #(.width(32)) register_10 (.D(I12), .en(we), .Q(O12), .clk(clk), .clr(reset));
  Register #(.width(32)) register_11 (.D(I13), .en(we), .Q(O13), .clk(clk), .clr(reset));
  Register #(.width(32)) register_12 (.D(I14), .en(we), .Q(O14), .clk(clk), .clr(reset));
  Register #(.width(32)) register_13 (.D(I15), .en(we), .Q(O15), .clk(clk), .clr(reset));
  Register #(.width(32)) register_14 (.D(I16), .en(we), .Q(O16), .clk(clk), .clr(reset));
  Register #(.width(32)) register_15 (.D(I17), .en(we), .Q(O17), .clk(clk), .clr(reset));
  Register #(.width(32)) register_16 (.D(I20), .en(we), .Q(O20), .clk(clk), .clr(reset));
  Register #(.width(32)) register_17 (.D(I21), .en(we), .Q(O21), .clk(clk), .clr(reset));
  Register #(.width(32)) register_18 (.D(I22), .en(we), .Q(O22), .clk(clk), .clr(reset));
  Register #(.width(32)) register_19 (.D(I23), .en(we), .Q(O23), .clk(clk), .clr(reset));
  Register #(.width(32)) register_20 (.D(I24), .en(we), .Q(O24), .clk(clk), .clr(reset));
  Register #(.width(32)) register_21 (.D(I25), .en(we), .Q(O25), .clk(clk), .clr(reset));
  Register #(.width(32)) register_22 (.D(I26), .en(we), .Q(O26), .clk(clk), .clr(reset));
  Register #(.width(32)) register_23 (.D(I27), .en(we), .Q(O27), .clk(clk), .clr(reset));
  Register #(.width(32)) register_24 (.D(I30), .en(we), .Q(O30), .clk(clk), .clr(reset));
  Register #(.width(32)) register_25 (.D(I31), .en(we), .Q(O31), .clk(clk), .clr(reset));
  Register #(.width(32)) register_26 (.D(I32), .en(we), .Q(O32), .clk(clk), .clr(reset));
  Register #(.width(32)) register_27 (.D(I33), .en(we), .Q(O33), .clk(clk), .clr(reset));
  Register #(.width(32)) register_28 (.D(I34), .en(we), .Q(O34), .clk(clk), .clr(reset));
  Register #(.width(32)) register_29 (.D(I35), .en(we), .Q(O35), .clk(clk), .clr(reset));
  Register #(.width(32)) register_30 (.D(I36), .en(we), .Q(O36), .clk(clk), .clr(reset));
  Register #(.width(32)) register_31 (.D(I37), .en(we), .Q(O37), .clk(clk), .clr(reset));
  Multiplexer #(.select(5), .width(32)) multiplexer_1 (
    .in0({32{1'b0}}), .in1(O01), .in2(O02), .in3(O03), .in4(O04), .in5(O05), .in6(O06), .in7(O07), .in8(O10),
    .in9(O11), .in10(O12), .in11(O13), .in12(O14), .in13(O15), .in14(O16), .in15(O17), .in16(O20),
    .in17(O21), .in18(O22), .in19(O23), .in20(O24), .in21(O25), .in22(O26), .in23(O27), .in24(O30),
    .in25(O31), .in26(O32), .in27(O33), .in28(O34), .in29(O35), .in30(O36), .in31(O37),
    .out(multiplexer_1_out), .sel(a1));  // open: en
  Multiplexer #(.select(5), .width(32)) multiplexer_2 (
    .in0({32{1'b0}}), .in1(O01), .in2(O02), .in3(O03), .in4(O04), .in5(O05), .in6(O06), .in7(O07), .in8(O10),
    .in9(O11), .in10(O12), .in11(O13), .in12(O14), .in13(O15), .in14(O16), .in15(O17), .in16(O20),
    .in17(O21), .in18(O22), .in19(O23), .in20(O24), .in21(O25), .in22(O26), .in23(O27), .in24(O30),
    .in25(O31), .in26(O32), .in27(O33), .in28(O34), .in29(O35), .in30(O36), .in31(O37),
    .out(multiplexer_2_out), .sel(a2));  // open: en
  Comparator #(.width(5)) comparator_1 (.a(a1), .b({5{1'b0}}), .eq(comparator_1_eq));  // open: gt, lt
  Comparator #(.width(5)) comparator_2 (.a(a1), .b(a3), .eq(comparator_2_eq));  // open: gt, lt
  Comparator #(.width(5)) comparator_3 (.a(a2), .b({5{1'b0}}), .eq(comparator_3_eq));  // open: gt, lt
  Comparator #(.width(5)) comparator_4 (.a(a2), .b(a3), .eq(comparator_4_eq));  // open: gt, lt
  not not_1 (not_1_out, comparator_1_eq);
  not not_2 (not_2_out, comparator_3_eq);
  and and_1 (and_1_out, not_1_out, comparator_2_eq, we);
  and and_2 (and_2_out, not_2_out, comparator_4_eq, we);
  Multiplexer #(.width(32)) multiplexer_3 (.in0(multiplexer_1_out), .in1(wd), .out(rd1), .sel(and_1_out));  // open: en
  Multiplexer #(.width(32)) multiplexer_4 (.in0(multiplexer_2_out), .in1(wd), .out(rd2), .sel(and_2_out));  // open: en
endmodule

module ALU (
  input  [31:0] a,
  input  [31:0] b,
  input  [1:0] op,
  output [31:0] c
);

  wire comparator_1_lt;
  wire [31:0] adder_1_out, bit_extender_1_out, or_1_out, subtractor_1_out;

  Comparator #(.width(32)) comparator_1 (.a(a), .b(b), .lt(comparator_1_lt));  // open: gt, eq
  Adder #(.width(32)) adder_1 (.a(a), .b(b), .out(adder_1_out));  // open: cin, cout
  Subtractor #(.width(32)) subtractor_1 (.a(a), .b(b), .out(subtractor_1_out));  // open: bin, bout
  assign bit_extender_1_out = {{31{1'b0}}, comparator_1_lt};  // Bit_Extender bit_extender_1
  assign or_1_out = a | b;  // OR_Gate or_1, 32 bits wide
  Multiplexer #(.select(2), .width(32)) multiplexer_1 (
    .in0(adder_1_out), .in1(subtractor_1_out), .in2(bit_extender_1_out), .in3(or_1_out), .out(c), .sel(op));  // open: en
endmodule

module DM (
  input  [31:0] address,
  input  [31:0] wd,
  input  we,
  input  clk,
  input  reset,
  output [31:0] rd
);

  wire [9:0] bit_extender_1_out;
  wire [31:0] shifter_1_out;

  Shifter #(.width(32), .shift("ar")) shifter_1 (.in(address), .\dist (5'b00010), .out(shifter_1_out));
  Bit_Extender #(.in_width(32), .out_width(10)) bit_extender_1 (.in(shifter_1_out), .out(bit_extender_1_out));
  RAM #(.addrWidth(10), .dataWidth(32), .bus("separate")) ram_1 (
    .addr(bit_extender_1_out), .din(wd), .data(rd), .str(we), .clk(clk), .ld(1'b1), .clr(reset));  // open: sel
endmodule

module PC (
  input  [31:0] di,
  input  CLK,
  input  CLR,
  output [31:0] \do 
);

  wire [31:0] subtractor_1_out;

  // Probe on subtractor_1_out[31:2]
  Subtractor #(.width(32)) subtractor_1 (.a(di), .b(32'h3000), .out(subtractor_1_out));  // open: bin, bout
  Register #(.width(30)) register_1 (.D(subtractor_1_out[31:2]), .Q(\do [31:2]), .clk(CLK), .clr(CLR));  // open: en

  assign \do [1:0] = 2'b00;
endmodule

module NPC (
  input  [31:0] pc,
  input  [31:0] offset,
  input  equal,
  input  be,
  output [31:0] cur,
  output [31:0] \new 
);

  wire [31:0] adder_2_out;

  Adder #(.width(32)) adder_1 (.a(pc), .b(32'h3004), .out(cur));  // open: cin, cout
  Adder #(.width(32)) adder_2 (.a(cur), .b(offset), .out(adder_2_out));  // open: cin, cout
  Multiplexer #(.select(2), .width(32)) multiplexer_1 (
    .in0(cur), .in1(adder_2_out), .in2(offset), .out(\new ), .sel({be, equal}));  // open: in3, en

  // Other names for the same wires on the sheet: J[31:0] = offset
endmodule

module IM (
  input  [31:0] pc,
  output [31:0] RD
);

  wire [9:0] bit_extender_1_out;
  wire [31:0] shifter_1_out;

  Shifter #(.width(32), .shift("ar")) shifter_1 (.in(pc), .\dist (5'b00010), .out(shifter_1_out));
  Bit_Extender #(.in_width(32), .out_width(10)) bit_extender_1 (.in(shifter_1_out), .out(bit_extender_1_out));
  ROM #(.addrWidth(10), .dataWidth(32)) rom_1 (.addr(bit_extender_1_out), .data(RD));  // open: sel

  // Notes on the sheet:
  //   contents of rom_1 (hex, n*v repeats v):
  //   8ee10000 243023 8ee50000 34a151e1 34030014 aee30000 8ee30000 8c650000 34040024 aee40000 8ee40000
  //   ac830000
endmodule

module IFU (
  input  clk,
  input  clr,
  input  [31:0] next,
  input  cmp,
  input  be,
  input  stall,
  output [5:0] func,
  output [4:0] shamt,
  output [4:0] rd,
  output [15:0] imm,
  output [4:0] rt,
  output [4:0] rs,
  output [5:0] op,
  output [25:0] _26imm,
  output [31:0] PC,
  output [31:0] instr
);

  wire [0:0] or_1_out;
  wire [31:0] adder_1_out, adder_2_out, multiplexer_1_out, multiplexer_2_out, pc_1_do, subtractor_1_out;

  Adder #(.width(32)) adder_1 (.a(pc_1_do), .b(32'h3004), .out(adder_1_out));  // open: cin, cout
  or or_1 (or_1_out[0], cmp, be);
  Multiplexer #(.select(2), .width(32)) multiplexer_1 (
    .in0(adder_1_out), .in1(next), .in2(pc_1_do), .in3(pc_1_do), .out(multiplexer_1_out),
    .sel({stall, or_1_out[0]}));  // open: en
  Multiplexer #(.width(32)) multiplexer_2 (
    .in0(multiplexer_1_out), .in1(adder_2_out), .out(multiplexer_2_out), .sel(be));  // open: en
  Adder #(.width(32)) adder_2 (.a(32'h4), .b(multiplexer_1_out), .out(adder_2_out));  // open: cin, cout
  PC pc_1 (.di(multiplexer_2_out), .CLK(clk), .CLR(clr), .\do (pc_1_do));
  Subtractor #(.width(32)) subtractor_1 (
    .a(multiplexer_1_out), .b(32'h3000), .out(subtractor_1_out));  // open: bin, bout
  // Probe on multiplexer_2_out
  Multiplexer #(.width(32)) multiplexer_3 (.in0(pc_1_do), .in1(subtractor_1_out), .out(PC), .sel(be));  // open: en
  IM im_1 (.pc(PC), .RD({instr[31:26], _26imm}));

  assign func = _26imm[5:0];
  assign imm = _26imm[15:0];
  assign instr[25:0] = _26imm;
  assign op = instr[31:26];
  assign rd = _26imm[15:11];
  assign rs = _26imm[25:21];
  assign rt = _26imm[20:16];
  assign shamt = _26imm[10:6];
endmodule

module main (
  input  reset,
  output [31:0] out_2,
  output [31:0] out_3,
  output grfWE,
  output [4:0] out_5,
  output [31:0] out_6,
  output out_7,
  output [31:0] out_8,
  output [31:0] out_9
);

  wire ALUd_E, be, clk, cmp, controller_1_alub, controller_1_dmwe, controller_1_grfwe, controller_1_tusers,
       controller_1_tuserse, controller_1_tuserte, d_reg_1_dmwe_2, Equal, grfWE_E, grfWE_M, offsetOp,
       stallOp, undriven;
  wire [1:0] aluop_E, controller_1_aluop, controller_1_grfa3op, controller_1_grfwdop, controller_1_tusert,
       ct_e_1_tnew, ct_m_1_tnew, d_reg_1_grfwop_2, grfA3op_E, grfA3op_M, grfA3op_W, grfWop_M, grfWop_W;
  wire [2:0] EXTmode;
  wire [4:0] grfWA_E, grfWA_M, ifu_1_rd, ifu_1_rs, ifu_1_rt, ifu_1_shamt, rd_D, rd_E, rd_M, rd_W, rs_D, rs_E,
       rs_M, rs_W, rt_D, rt_E, rt_M, rt_W, shamt_D;
  wire [5:0] d_reg_1_func_2, d_reg_1_op_2, e_reg_1_func_2, e_reg_1_op_2, func_D, ifu_1_func, ifu_1_op, op_D;
  wire [15:0] ifu_1_imm, imm_D;
  wire [25:0] _26imm_D, ifu_1__26imm;
  wire [31:0] adder_1_out, adder_2_out, alu_1_c, ALUans_W, b, d_reg_1_pc_4_2, DMRD_M, DMRD_W, Ext_D, Ext_E,
       Ext_M, Ext_W, fwd_4_o, fwd_5_o, grfW_M, ifu_1_pc, Instr, newpc, offset, PC_4_D, PC_4_M, PC_4_W, pc_D,
       RD1_D, rd1_D_t, rd1_E, RD2_D, rd2_D_t, RD2_E, rd2_E_t;

  Clock clock_1 (.out(clk));
  Subtractor #(.width(32)) subtractor_1 (.a(PC_4_W), .b(32'h4), .out(out_2));  // open: bin, bout
  Subtractor #(.width(32)) subtractor_2 (.a(PC_4_M), .b(32'h4), .out(out_3));  // open: bin, bout
  IFU ifu_1 (
    .clk(clk), .clr(reset), .func(ifu_1_func), .shamt(ifu_1_shamt), .rd(ifu_1_rd), .rt(ifu_1_rt),
    .rs(ifu_1_rs), .op(ifu_1_op), .imm(ifu_1_imm), ._26imm(ifu_1__26imm), .instr(Instr), .PC(ifu_1_pc),
    .next(newpc), .be(be), .stall(stallOp), .cmp(cmp));
  F_REG f_reg_1 (
    .func(ifu_1_func), .shamt(ifu_1_shamt), .rd(ifu_1_rd), .rt(ifu_1_rt), .rs(ifu_1_rs), .op(ifu_1_op),
    .imm(ifu_1_imm), ._26imm(ifu_1__26imm), .pc(ifu_1_pc), .func_2(func_D), .shamt_2(shamt_D), .rd_2(rd_D),
    .rt_2(rt_D), .rs_2(rs_D), .op_2(op_D), .imm_2(imm_D), ._26imm_2(_26imm_D), .pc_2(pc_D), .clk(clk),
    .clr(reset), .stall(stallOp));
  // Probe on pc_D
  FWD fwd_1 (
    .rd(rd1_D_t), .ra(rs_D), .d1(rd2_E_t), .we1(grfWE_E), .d2(grfW_M), .src1(rt_E), .we2(grfWE_M),
    .src2(grfWA_M), .o(RD1_D));
  FWD fwd_2 (
    .rd(rd2_D_t), .ra(rt_D), .d1(rd2_E_t), .we1(grfWE_E), .d2(grfW_M), .src1(rt_E), .we2(grfWE_M),
    .src2(grfWA_M), .o(RD2_D));
  Controller controller_1 (
    .func(func_D), .grfWe(controller_1_grfwe), .aluB(controller_1_alub), .aluOp(controller_1_aluop),
    .dpMode(EXTmode), .DMWE(controller_1_dmwe), .grfA3Op(controller_1_grfa3op), .cmp(cmp),
    .grfWdOp(controller_1_grfwdop), .be(be), .offsetOp(offsetOp), .tUseRs(controller_1_tusers),
    .tUseRsE(controller_1_tuserse), .tUseRt(controller_1_tusert), .tUseRtE(controller_1_tuserte), .op(op_D));
  GRF grf_1 (
    .a1(rs_D), .a2(rt_D), .wd(out_6), .rd1(rd1_D_t), .rd2(rd2_D_t), .clk(clk), .we(grfWE), .a3(out_5),
    .reset(reset));
  SCT sct_1 (
    .tUseRsDEn(controller_1_tuserse), .tUseRsD(controller_1_tusers), .rsD(rs_D),
    .tUseRtDEn(controller_1_tuserte), .tUseRtD(controller_1_tusert), .rtD(rt_D), .tNewE(ct_e_1_tnew),
    .EwE(grfWE_E), .EWA(grfWA_E), .tNewM(ct_m_1_tnew), .MwE(grfWE_M), .MWA(grfWA_M), .stall(stallOp));
  CMP cmp_1 (.cmp(cmp), .a(RD1_D), .b(RD2_D), .equal(Equal));
  NPC npc_1 (.\new (newpc), .cur(PC_4_D), .pc(pc_D), .offset(offset), .equal(Equal), .be(be));
  Multiplexer #(.width(32)) multiplexer_1 (.in0(Ext_D), .in1(RD1_D), .out(offset), .sel(offsetOp));  // open: en
  EXT ext_1 (.IMM(imm_D), .EXTmode(EXTmode), .Ext(Ext_D), .imm26(_26imm_D), .PC(PC_4_D), .grfRs(RD1_D));
  D_REG d_reg_1 (
    .grf_WE(controller_1_grfwe), .aluOp(controller_1_aluop), .aluD(controller_1_alub),
    .dmWE(controller_1_dmwe), .grfWOp(controller_1_grfwdop), .rd1(RD1_D), .rd2(RD2_D), .ext(Ext_D),
    .grf_WE_2(grfWE_E), .aluOp_2(aluop_E), .aluD_2(ALUd_E), .dmWE_2(d_reg_1_dmwe_2),
    .grfWOp_2(d_reg_1_grfwop_2), .rd1_2(rd1_E), .rd2_2(rd2_E_t), .ext_2(Ext_E), .in_3(clk), .in_1(reset),
    .grfA3Op(controller_1_grfa3op), .grfA3Op_2(grfA3op_E), .rd(rd_D), .rt(rt_D), .rt_2(rt_E), .rd_2(rd_E),
    .pc_4(PC_4_D), .pc_4_2(d_reg_1_pc_4_2), .op(op_D), .func(func_D), .op_2(d_reg_1_op_2),
    .func_2(d_reg_1_func_2), .stall(stallOp), .rs(rs_D), .rs_2(rs_E));
  CT_E ct_e_1 (
    .op(d_reg_1_op_2), .func(d_reg_1_func_2), .tNew(ct_e_1_tnew));  // open: tUseRs, tUseRsE, tUseRt, tUseRtE, tNewE
  FWD fwd_3 (
    .rd(rd2_E_t), .ra(rt_E), .d1(out_8), .we1(grfWE_M), .d2(out_6), .src1(grfWA_M), .we2(grfWE),
    .src2(out_5), .o(RD2_E));
  Multiplexer #(.width(32)) multiplexer_2 (.in0(RD2_E), .in1(Ext_E), .out(b), .sel(ALUd_E), .en(undriven));
  // Probe on d_reg_1_pc_4_2
  Multiplexer #(.select(2), .width(5)) multiplexer_3 (
    .in0(rd_E), .in1(rt_E), .in2({5{1'b1}}), .out(grfWA_E), .sel(grfA3op_E));  // open: in3, en
  FWD fwd_4 (
    .rd(rd1_E), .ra(rs_E), .d1(out_8), .we1(grfWE_M), .d2(out_6), .src1(grfWA_M), .we2(grfWE), .src2(out_5),
    .o(fwd_4_o));
  E_REG e_reg_1 (
    .grf_WE(grfWE_E), .dmWE(d_reg_1_dmwe_2), .grfA3Op(grfA3op_E), .grfWOp(d_reg_1_grfwop_2),
    .aluAns(alu_1_c), .rd2(RD2_E), .rt(rt_E), .rd(rd_E), .pc_4(d_reg_1_pc_4_2), .ext(Ext_E),
    .grf_WE_2(grfWE_M), .dmWE_2(out_7), .grfA3Op_2(grfA3op_M), .grfWOp_2(grfWop_M), .aluAns_2(out_8),
    .rd2_2(out_9), .rt_2(rt_M), .rd_2(rd_M), .pc_4_2(PC_4_M), .ext_2(Ext_M), .clk(clk), .clr(reset),
    .op(d_reg_1_op_2), .op_2(e_reg_1_op_2), .func(d_reg_1_func_2), .func_2(e_reg_1_func_2), .rs(rs_E),
    .rs_2(rs_M));
  ALU alu_1 (.a(fwd_4_o), .b(b), .op(aluop_E), .c(alu_1_c));
  CT_M ct_m_1 (
    .opcode(e_reg_1_op_2), .func(e_reg_1_func_2), .tNew(ct_m_1_tnew));  // open: tUseRs, tUseRsE, tUseRt, tUseRtE, tNewE
  Multiplexer #(.select(2), .width(5)) multiplexer_4 (
    .in0(rd_M), .in1(rt_M), .in2({5{1'b1}}), .out(grfWA_M), .sel(grfA3op_M));  // open: in3, en
  Adder #(.width(32)) adder_1 (.a(PC_4_M), .b(32'h4), .out(adder_1_out));  // open: cin, cout
  FWD fwd_5 (
    .rd(out_9), .ra(rt_M), .d1(out_6), .we1(grfWE), .d2({32{1'b0}}), .src1(out_5), .we2(1'b0),
    .src2({5{1'b0}}), .o(fwd_5_o));
  DM dm_1 (.address(out_8), .wd(fwd_5_o), .we(out_7), .reset(reset), .rd(DMRD_M), .clk(clk));
  Multiplexer #(.select(2), .width(5)) multiplexer_5 (
    .in0(rd_M), .in1(rt_M), .in2({5{1'b1}}), .out(grfWA_M), .sel(grfA3op_M));  // open: in3, en
  Multiplexer #(.select(2), .width(32)) multiplexer_6 (
    .in0(out_8), .in1(DMRD_M), .in2(Ext_M), .in3(adder_1_out), .out(grfW_M), .sel(grfWop_M));  // open: en
  M_REG m_reg_1 (
    .grf_WE(grfWE_M), .grfA3Op(grfA3op_M), .grfWOp(grfWop_M), .DMRd(DMRD_M), .aluAns(out_8), .rt(rt_M),
    .rd(rd_M), .pc_4(PC_4_M), .ext(Ext_M), .grf_WE_2(grfWE), .grfA3Op_2(grfA3op_W), .grfWOp_2(grfWop_W),
    .DMRd_2(DMRD_W), .aluAns_2(ALUans_W), .rt_3(rt_W), .rd_2(rd_W), .pc_4_2(PC_4_W), .ext_2(Ext_W),
    .clk(clk), .clr(reset), .op(e_reg_1_op_2), .func(e_reg_1_func_2), .rs(rs_M), .rt_2(rs_W));  // open: op_2, func_2
  Multiplexer #(.select(2), .width(5)) multiplexer_7 (
    .in0(rd_W), .in1(rt_W), .in2({5{1'b1}}), .out(out_5), .sel(grfA3op_W));  // open: in3, en
  Adder #(.width(32)) adder_2 (.a(PC_4_W), .b(32'h4), .out(adder_2_out));  // open: cin, cout
  Multiplexer #(.select(2), .width(32)) multiplexer_8 (
    .in0(ALUans_W), .in1(DMRD_W), .in2(Ext_W), .in3(adder_2_out), .out(out_6), .sel(grfWop_W));  // open: en

  // Other names for the same wires on the sheet: ALUans_M[31:0] = out_8; dmWE_M = out_7; grfW[31:0] = out_6;
  //   grfWA[4:0] = out_5; rd2_M[31:0] = out_9
endmodule

module Controller (
  input  [5:0] op,
  input  [5:0] func,
  output grfWe,
  output [1:0] aluOp,
  output aluB,
  output tUseRs,
  output DMWE,
  output [2:0] dpMode,
  output cmp,
  output tUseRsE,
  output be,
  output offsetOp,
  output [1:0] grfWdOp,
  output [1:0] tUseRt,
  output tUseRtE,
  output [1:0] grfA3Op
);

  wire addu, beq, comparator_2_eq, comparator_3_eq, comparator_4_eq, comparator_5_eq, comparator_6_eq, j,
       jal, jalr, jr, lui, lw, ori, R_type, slt, subu, sw;

  Comparator #(.width(6)) comparator_1 (.a(op), .b({6{1'b0}}), .eq(R_type));  // open: gt, lt
  Comparator #(.width(6)) comparator_2 (.a(func), .b(6'b100001), .eq(comparator_2_eq));  // open: gt, lt
  Comparator #(.width(6)) comparator_3 (.a(func), .b(6'b100011), .eq(comparator_3_eq));  // open: gt, lt
  Comparator #(.width(6)) comparator_4 (.a(func), .b(6'b101010), .eq(comparator_4_eq));  // open: gt, lt
  Comparator #(.width(6)) comparator_5 (.a(func), .b(6'b001001), .eq(comparator_5_eq));  // open: gt, lt
  Comparator #(.width(6)) comparator_6 (.a(func), .b(6'b001000), .eq(comparator_6_eq));  // open: gt, lt
  and and_1 (addu, comparator_2_eq, R_type);
  and and_2 (subu, comparator_3_eq, R_type);
  and and_3 (slt, comparator_4_eq, R_type);
  and and_4 (jalr, comparator_5_eq, R_type);
  and and_5 (jr, comparator_6_eq, R_type);
  Comparator #(.width(6)) comparator_7 (.a(op), .b(6'b001101), .eq(ori));  // open: gt, lt
  Comparator #(.width(6)) comparator_8 (.a(op), .b(6'b100011), .eq(lw));  // open: gt, lt
  Comparator #(.width(6)) comparator_9 (.a(op), .b(6'b101011), .eq(sw));  // open: gt, lt
  Comparator #(.width(6)) comparator_10 (.a(op), .b(6'b000100), .eq(beq));  // open: gt, lt
  Comparator #(.width(6)) comparator_11 (.a(op), .b(6'b001111), .eq(lui));  // open: gt, lt
  Comparator #(.width(6)) comparator_12 (.a(op), .b(6'b000011), .eq(jal));  // open: gt, lt
  Comparator #(.width(6)) comparator_13 (.a(op), .b(6'b000010), .eq(j));  // open: gt, lt
  or or_1 (grfWe, jal, addu, subu, ori, lw, lui, slt, jalr);
  or or_2 (aluB, ori, lw, sw);
  buf or_3 (DMWE, sw);  // OR_Gate
  buf or_4 (cmp, beq);  // OR_Gate
  or or_5 (be, jal, j, jr);
  buf or_6 (offsetOp, jr);  // OR_Gate
  or or_7 (aluOp[0], subu, ori, beq);
  or or_8 (aluOp[1], ori, slt);
  or or_9 (dpMode[0], lw, sw, lui, jalr);
  or or_10 (dpMode[1], beq, lui);
  or or_11 (dpMode[2], jal, jalr, j);
  or or_12 (grfWdOp[0], lw, jal, jalr);
  or or_13 (grfWdOp[1], lui, jal, jalr);
  or or_14 (grfA3Op[0], lw, ori, lui);
  buf or_15 (grfA3Op[1], jal);  // OR_Gate
  or or_16 (tUseRs, addu, subu, ori, lw, sw);
  or or_17 (tUseRsE, beq, addu, subu, ori, lw, sw, jr);
  or or_18 (tUseRt[0], addu, subu);
  buf or_19 (tUseRt[1], sw);  // OR_Gate
  or or_20 (tUseRtE, addu, subu, sw, beq);
endmodule

module EXT (
  input  [25:0] imm26,
  input  [31:0] PC,
  input  [15:0] IMM,
  input  [2:0] EXTmode,
  input  [31:0] grfRs,
  output [31:0] Ext
);

  wire [31:0] bit_extender_1_out, bit_extender_2_out, bit_extender_3_out;

  assign bit_extender_1_out = {{16{1'b0}}, IMM};  // Bit_Extender bit_extender_1
  assign bit_extender_2_out = {{16{IMM[15]}}, IMM};  // Bit_Extender bit_extender_2
  assign bit_extender_3_out = {{14{IMM[15]}}, {IMM, 2'b00}};  // Bit_Extender bit_extender_3
  Multiplexer #(.select(3), .width(32)) multiplexer_1 (
    .in0(bit_extender_1_out), .in1(bit_extender_2_out), .in2(bit_extender_3_out), .in3({IMM, {16{1'b0}}}),
    .in4({PC[31:28], imm26, 2'b00}), .in5(grfRs), .out(Ext), .sel(EXTmode));  // open: in6, in7, en
endmodule

module F_REG (
  input  stall,
  input  clk,
  input  clr,
  input  [5:0] func,
  input  [4:0] shamt,
  input  [4:0] rd,
  input  [4:0] rt,
  input  [4:0] rs,
  input  [5:0] op,
  input  [15:0] imm,
  input  [25:0] _26imm,
  input  [31:0] pc,
  output [5:0] func_2,
  output [4:0] shamt_2,
  output [4:0] rd_2,
  output [4:0] rt_2,
  output [4:0] rs_2,
  output [5:0] op_2,
  output [15:0] imm_2,
  output [25:0] _26imm_2,
  output [31:0] pc_2
);

  wire not_1_out;

  not not_1 (not_1_out, stall);
  Register #(.width(6)) register_1 (.D(func), .en(not_1_out), .Q(func_2), .clk(clk), .clr(clr));
  Register #(.width(5)) register_2 (.D(shamt), .en(not_1_out), .Q(shamt_2), .clk(clk), .clr(clr));
  Register #(.width(5)) register_3 (.D(rd), .en(not_1_out), .Q(rd_2), .clk(clk), .clr(clr));
  Register #(.width(5)) register_4 (.D(rt), .en(not_1_out), .Q(rt_2), .clk(clk), .clr(clr));
  Register #(.width(5)) register_5 (.D(rs), .en(not_1_out), .Q(rs_2), .clk(clk), .clr(clr));
  Register #(.width(6)) register_6 (.D(op), .en(not_1_out), .Q(op_2), .clk(clk), .clr(clr));
  Register #(.width(16)) register_7 (.D(imm), .en(not_1_out), .Q(imm_2), .clk(clk), .clr(clr));
  Register #(.width(26)) register_8 (.D(_26imm), .en(not_1_out), .Q(_26imm_2), .clk(clk), .clr(clr));
  Register #(.width(32)) register_9 (.D(pc), .en(not_1_out), .Q(pc_2), .clk(clk), .clr(clr));
endmodule

module D_REG (
  input  in_1,
  input  stall,
  input  in_3,
  input  grf_WE,
  input  [1:0] aluOp,
  input  aluD,
  input  dmWE,
  input  [1:0] grfA3Op,
  input  [1:0] grfWOp,
  input  [31:0] rd1,
  input  [31:0] rd2,
  input  [4:0] rs,
  input  [4:0] rt,
  input  [4:0] rd,
  input  [31:0] pc_4,
  input  [31:0] ext,
  input  [5:0] op,
  input  [5:0] func,
  output grf_WE_2,
  output [1:0] aluOp_2,
  output aluD_2,
  output dmWE_2,
  output [1:0] grfA3Op_2,
  output [1:0] grfWOp_2,
  output [31:0] rd1_2,
  output [31:0] rd2_2,
  output [4:0] rs_2,
  output [4:0] rt_2,
  output [4:0] rd_2,
  output [31:0] pc_4_2,
  output [31:0] ext_2,
  output [5:0] op_2,
  output [5:0] func_2
);

  wire re, register_16_q;

  or or_1 (re, in_1, stall);
  Register #(.width(1)) register_1 (.D(grf_WE), .en(1'b1), .Q(grf_WE_2), .clk(in_3), .clr(register_16_q));
  Register #(.width(2)) register_2 (.D(aluOp), .en(1'b1), .Q(aluOp_2), .clk(in_3), .clr(register_16_q));
  Register #(.width(1)) register_3 (.D(aluD), .en(1'b1), .Q(aluD_2), .clk(in_3), .clr(register_16_q));
  Register #(.width(1)) register_4 (.D(dmWE), .en(1'b1), .Q(dmWE_2), .clk(in_3), .clr(register_16_q));
  Register #(.width(2)) register_5 (.D(grfA3Op), .en(1'b1), .Q(grfA3Op_2), .clk(in_3), .clr(register_16_q));
  Register #(.width(2)) register_6 (.D(grfWOp), .en(1'b1), .Q(grfWOp_2), .clk(in_3), .clr(register_16_q));
  Register #(.width(32)) register_7 (.D(rd1), .en(1'b1), .Q(rd1_2), .clk(in_3), .clr(register_16_q));
  Register #(.width(32)) register_8 (.D(rd2), .en(1'b1), .Q(rd2_2), .clk(in_3), .clr(register_16_q));
  Register #(.width(5)) register_9 (.D(rs), .en(1'b1), .Q(rs_2), .clk(in_3), .clr(register_16_q));
  Register #(.width(5)) register_10 (.D(rt), .en(1'b1), .Q(rt_2), .clk(in_3), .clr(register_16_q));
  Register #(.width(5)) register_11 (.D(rd), .en(1'b1), .Q(rd_2), .clk(in_3), .clr(register_16_q));
  Register #(.width(32)) register_12 (.D(pc_4), .en(1'b1), .Q(pc_4_2), .clk(in_3), .clr(register_16_q));
  Register #(.width(32)) register_13 (.D(ext), .en(1'b1), .Q(ext_2), .clk(in_3), .clr(register_16_q));
  Register #(.width(6)) register_14 (.D(op), .en(1'b1), .Q(op_2), .clk(in_3), .clr(register_16_q));
  Register #(.width(6)) register_15 (.D(func), .en(1'b1), .Q(func_2), .clk(in_3), .clr(register_16_q));
  Register #(.width(1)) register_16 (.D(re), .en(1'b1), .Q(register_16_q), .clk(in_3), .clr(register_16_q));
endmodule

module E_REG (
  input  clk,
  input  clr,
  input  grf_WE,
  input  dmWE,
  input  [1:0] grfA3Op,
  input  [1:0] grfWOp,
  input  [31:0] aluAns,
  input  [31:0] rd2,
  input  [4:0] rs,
  input  [4:0] rt,
  input  [4:0] rd,
  input  [31:0] pc_4,
  input  [31:0] ext,
  input  [5:0] op,
  input  [5:0] func,
  output grf_WE_2,
  output dmWE_2,
  output [1:0] grfA3Op_2,
  output [1:0] grfWOp_2,
  output [31:0] aluAns_2,
  output [31:0] rd2_2,
  output [4:0] rs_2,
  output [4:0] rt_2,
  output [4:0] rd_2,
  output [31:0] pc_4_2,
  output [31:0] ext_2,
  output [5:0] op_2,
  output [5:0] func_2
);

  Register #(.width(1)) register_1 (.D(grf_WE), .en(1'b1), .Q(grf_WE_2), .clk(clk), .clr(clr));
  Register #(.width(1)) register_2 (.D(dmWE), .en(1'b1), .Q(dmWE_2), .clk(clk), .clr(clr));
  Register #(.width(2)) register_3 (.D(grfA3Op), .en(1'b1), .Q(grfA3Op_2), .clk(clk), .clr(clr));
  Register #(.width(2)) register_4 (.D(grfWOp), .en(1'b1), .Q(grfWOp_2), .clk(clk), .clr(clr));
  Register #(.width(32)) register_5 (.D(aluAns), .en(1'b1), .Q(aluAns_2), .clk(clk), .clr(clr));
  Register #(.width(32)) register_6 (.D(rd2), .en(1'b1), .Q(rd2_2), .clk(clk), .clr(clr));
  Register #(.width(5)) register_7 (.D(rs), .en(1'b1), .Q(rs_2), .clk(clk), .clr(clr));
  Register #(.width(5)) register_8 (.D(rt), .en(1'b1), .Q(rt_2), .clk(clk), .clr(clr));
  Register #(.width(5)) register_9 (.D(rd), .en(1'b1), .Q(rd_2), .clk(clk), .clr(clr));
  Register #(.width(32)) register_10 (.D(pc_4), .en(1'b1), .Q(pc_4_2), .clk(clk), .clr(clr));
  Register #(.width(32)) register_11 (.D(ext), .en(1'b1), .Q(ext_2), .clk(clk), .clr(clr));
  Register #(.width(6)) register_12 (.D(op), .en(1'b1), .Q(op_2), .clk(clk), .clr(clr));
  Register #(.width(6)) register_13 (.D(func), .en(1'b1), .Q(func_2), .clk(clk), .clr(clr));
endmodule

module M_REG (
  input  clk,
  input  clr,
  input  grf_WE,
  input  [1:0] grfA3Op,
  input  [1:0] grfWOp,
  input  [31:0] DMRd,
  input  [31:0] aluAns,
  input  [4:0] rs,
  input  [4:0] rt,
  input  [4:0] rd,
  input  [31:0] pc_4,
  input  [31:0] ext,
  input  [5:0] op,
  input  [5:0] func,
  output grf_WE_2,
  output [1:0] grfA3Op_2,
  output [1:0] grfWOp_2,
  output [31:0] DMRd_2,
  output [31:0] aluAns_2,
  output [4:0] rt_2,
  output [4:0] rt_3,
  output [4:0] rd_2,
  output [31:0] pc_4_2,
  output [31:0] ext_2,
  output [5:0] op_2,
  output [5:0] func_2
);

  Register #(.width(1)) register_1 (.D(grf_WE), .en(1'b1), .Q(grf_WE_2), .clk(clk), .clr(clr));
  Register #(.width(2)) register_2 (.D(grfA3Op), .en(1'b1), .Q(grfA3Op_2), .clk(clk), .clr(clr));
  Register #(.width(2)) register_3 (.D(grfWOp), .en(1'b1), .Q(grfWOp_2), .clk(clk), .clr(clr));
  Register #(.width(32)) register_4 (.D(DMRd), .en(1'b1), .Q(DMRd_2), .clk(clk), .clr(clr));
  Register #(.width(32)) register_5 (.D(aluAns), .en(1'b1), .Q(aluAns_2), .clk(clk), .clr(clr));
  Register #(.width(5)) register_6 (.D(rs), .en(1'b1), .Q(rt_2), .clk(clk), .clr(clr));
  Register #(.width(5)) register_7 (.D(rt), .en(1'b1), .Q(rt_3), .clk(clk), .clr(clr));
  Register #(.width(5)) register_8 (.D(rd), .en(1'b1), .Q(rd_2), .clk(clk), .clr(clr));
  Register #(.width(32)) register_9 (.D(pc_4), .en(1'b1), .Q(pc_4_2), .clk(clk), .clr(clr));
  Register #(.width(32)) register_10 (.D(ext), .en(1'b1), .Q(ext_2), .clk(clk), .clr(clr));
  Register #(.width(6)) register_11 (.D(op), .en(1'b1), .Q(op_2), .clk(clk), .clr(clr));
  Register #(.width(6)) register_12 (.D(func), .en(1'b1), .Q(func_2), .clk(clk), .clr(clr));
endmodule

module CMP (
  input  cmp,
  input  [31:0] a,
  input  [31:0] b,
  output equal
);

  wire comparator_1_eq;

  and and_1 (equal, cmp, comparator_1_eq);
  Comparator #(.width(32)) comparator_1 (.a(a), .b(b), .eq(comparator_1_eq));  // open: gt, lt
endmodule

module CT_E (
  input  [5:0] op,
  input  [5:0] func,
  output tUseRs,
  output tUseRsE,
  output [1:0] tUseRt,
  output tUseRtE,
  output [1:0] tNew,
  output tNewE
);

  wire addu, beq, comparator_2_eq, comparator_3_eq, comparator_4_eq, comparator_5_eq, comparator_6_eq, j,
       jal, jalr, jr, lui, lw, ori, R_type, slt, subu, sw;

  Comparator #(.width(6)) comparator_1 (.a(op), .b({6{1'b0}}), .eq(R_type));  // open: gt, lt
  Comparator #(.width(6)) comparator_2 (.a(func), .b(6'b100001), .eq(comparator_2_eq));  // open: gt, lt
  Comparator #(.width(6)) comparator_3 (.a(func), .b(6'b100011), .eq(comparator_3_eq));  // open: gt, lt
  Comparator #(.width(6)) comparator_4 (.a(func), .b(6'b101010), .eq(comparator_4_eq));  // open: gt, lt
  Comparator #(.width(6)) comparator_5 (.a(func), .b(6'b001001), .eq(comparator_5_eq));  // open: gt, lt
  Comparator #(.width(6)) comparator_6 (.a(func), .b(6'b001000), .eq(comparator_6_eq));  // open: gt, lt
  and and_1 (addu, comparator_2_eq, R_type);
  and and_2 (subu, comparator_3_eq, R_type);
  and and_3 (slt, comparator_4_eq, R_type);
  and and_4 (jalr, comparator_5_eq, R_type);
  and and_5 (jr, comparator_6_eq, R_type);
  Comparator #(.width(6)) comparator_7 (.a(op), .b(6'b001101), .eq(ori));  // open: gt, lt
  Comparator #(.width(6)) comparator_8 (.a(op), .b(6'b100011), .eq(lw));  // open: gt, lt
  Comparator #(.width(6)) comparator_9 (.a(op), .b(6'b101011), .eq(sw));  // open: gt, lt
  Comparator #(.width(6)) comparator_10 (.a(op), .b(6'b000100), .eq(beq));  // open: gt, lt
  Comparator #(.width(6)) comparator_11 (.a(op), .b(6'b001111), .eq(lui));  // open: gt, lt
  Comparator #(.width(6)) comparator_12 (.a(op), .b(6'b000011), .eq(jal));  // open: gt, lt
  Comparator #(.width(6)) comparator_13 (.a(op), .b(6'b000010), .eq(j));  // open: gt, lt
  or or_1 (tUseRsE, addu, subu, ori, lw, sw);
  buf or_2 (tUseRt[0], sw);  // OR_Gate
  or or_3 (tUseRtE, addu, subu, sw);
  or or_4 (tNew[0], addu, subu, ori, lui);
  buf or_5 (tNew[1], lw);  // OR_Gate
  or or_6 (tNewE, addu, subu, ori, lui, lw, jal);

  assign tUseRs = 1'b0;
  assign tUseRt[1] = 1'b0;
endmodule

module CT_M (
  input  [5:0] opcode,
  input  [5:0] func,
  output tUseRs,
  output tUseRsE,
  output [1:0] tUseRt,
  output tUseRtE,
  output [1:0] tNew,
  output tNewE
);

  wire addu, beq, comparator_2_eq, comparator_3_eq, comparator_4_eq, comparator_5_eq, comparator_6_eq, j,
       jal, jalr, jr, lui, lw, ori, R_type, slt, subu, sw;

  Comparator #(.width(6)) comparator_1 (.a(opcode), .b({6{1'b0}}), .eq(R_type));  // open: gt, lt
  Comparator #(.width(6)) comparator_2 (.a(func), .b(6'b100001), .eq(comparator_2_eq));  // open: gt, lt
  Comparator #(.width(6)) comparator_3 (.a(func), .b(6'b100011), .eq(comparator_3_eq));  // open: gt, lt
  Comparator #(.width(6)) comparator_4 (.a(func), .b(6'b101010), .eq(comparator_4_eq));  // open: gt, lt
  Comparator #(.width(6)) comparator_5 (.a(func), .b(6'b001001), .eq(comparator_5_eq));  // open: gt, lt
  Comparator #(.width(6)) comparator_6 (.a(func), .b(6'b001000), .eq(comparator_6_eq));  // open: gt, lt
  and and_1 (addu, comparator_2_eq, R_type);
  and and_2 (subu, comparator_3_eq, R_type);
  and and_3 (slt, comparator_4_eq, R_type);
  and and_4 (jalr, comparator_5_eq, R_type);
  and and_5 (jr, comparator_6_eq, R_type);
  Comparator #(.width(6)) comparator_7 (.a(opcode), .b(6'b001101), .eq(ori));  // open: gt, lt
  Comparator #(.width(6)) comparator_8 (.a(opcode), .b(6'b100011), .eq(lw));  // open: gt, lt
  Comparator #(.width(6)) comparator_9 (.a(opcode), .b(6'b101011), .eq(sw));  // open: gt, lt
  Comparator #(.width(6)) comparator_10 (.a(opcode), .b(6'b000100), .eq(beq));  // open: gt, lt
  Comparator #(.width(6)) comparator_11 (.a(opcode), .b(6'b001111), .eq(lui));  // open: gt, lt
  Comparator #(.width(6)) comparator_12 (.a(opcode), .b(6'b000011), .eq(jal));  // open: gt, lt
  Comparator #(.width(6)) comparator_13 (.a(opcode), .b(6'b000010), .eq(j));  // open: gt, lt
  buf or_1 (tUseRtE, sw);  // OR_Gate
  buf or_2 (tNew[0], lw);  // OR_Gate
  or or_3 (tNewE, addu, subu, ori, lui, lw);

  assign tNew[1] = 1'b0;
  assign tUseRs = 1'b0;
  assign tUseRsE = 1'b0;
  assign tUseRt = 2'b00;

  // Other names for the same wires on the sheet: op[5:0] = opcode
endmodule

module CT_W (
  input  [5:0] opcode,
  input  [5:0] func,
  output tUseRs,
  output tUseRsE,
  output [1:0] tUseRt,
  output tUseRtE,
  output [1:0] tNew,
  output tNewE
);

  wire addu, beq, comparator_2_eq, comparator_3_eq, comparator_4_eq, comparator_5_eq, comparator_6_eq, j,
       jal, jalr, jr, lui, lw, ori, R_type, slt, subu, sw;

  Comparator #(.width(6)) comparator_1 (.a(opcode), .b({6{1'b0}}), .eq(R_type));  // open: gt, lt
  Comparator #(.width(6)) comparator_2 (.a(func), .b(6'b100001), .eq(comparator_2_eq));  // open: gt, lt
  Comparator #(.width(6)) comparator_3 (.a(func), .b(6'b100011), .eq(comparator_3_eq));  // open: gt, lt
  Comparator #(.width(6)) comparator_4 (.a(func), .b(6'b101010), .eq(comparator_4_eq));  // open: gt, lt
  Comparator #(.width(6)) comparator_5 (.a(func), .b(6'b001001), .eq(comparator_5_eq));  // open: gt, lt
  Comparator #(.width(6)) comparator_6 (.a(func), .b(6'b001000), .eq(comparator_6_eq));  // open: gt, lt
  and and_1 (addu, comparator_2_eq, R_type);
  and and_2 (subu, comparator_3_eq, R_type);
  and and_3 (slt, comparator_4_eq, R_type);
  and and_4 (jalr, comparator_5_eq, R_type);
  and and_5 (jr, comparator_6_eq, R_type);
  Comparator #(.width(6)) comparator_7 (.a(opcode), .b(6'b001101), .eq(ori));  // open: gt, lt
  Comparator #(.width(6)) comparator_8 (.a(opcode), .b(6'b100011), .eq(lw));  // open: gt, lt
  Comparator #(.width(6)) comparator_9 (.a(opcode), .b(6'b101011), .eq(sw));  // open: gt, lt
  Comparator #(.width(6)) comparator_10 (.a(opcode), .b(6'b000100), .eq(beq));  // open: gt, lt
  Comparator #(.width(6)) comparator_11 (.a(opcode), .b(6'b001111), .eq(lui));  // open: gt, lt
  Comparator #(.width(6)) comparator_12 (.a(opcode), .b(6'b000011), .eq(jal));  // open: gt, lt
  Comparator #(.width(6)) comparator_13 (.a(opcode), .b(6'b000010), .eq(j));  // open: gt, lt
  buf or_1 (tNewE, lw);  // OR_Gate

  assign tNew = 2'b00;
  assign tUseRs = 1'b0;
  assign tUseRsE = 1'b0;
  assign tUseRt = 2'b00;
  assign tUseRtE = 1'b0;

  // Other names for the same wires on the sheet: op[5:0] = opcode
endmodule

module SCT (
  input  tUseRsDEn,
  input  tUseRsD,
  input  [4:0] rsD,
  input  tUseRtDEn,
  input  [1:0] tUseRtD,
  input  [4:0] rtD,
  input  [1:0] tNewE,
  input  EwE,
  input  [4:0] EWA,
  input  [1:0] tNewM,
  input  MwE,
  input  [4:0] MWA,
  output stall
);

  wire and_1_out, and_2_out, and_3_out, and_4_out, comparator_1_eq, comparator_2_eq, comparator_3_gt,
       comparator_4_eq, comparator_5_eq, comparator_6_gt, comparator_7_eq, comparator_8_eq, comparator_9_gt,
       comparator_10_eq, comparator_11_eq, comparator_12_gt, not_1_out, not_2_out, not_3_out, not_4_out;
  wire [1:0] bit_extender_1_out, bit_extender_2_out;

  assign bit_extender_1_out = {{1{1'b0}}, tUseRsD};  // Bit_Extender bit_extender_1
  assign bit_extender_2_out = {{1{1'b0}}, tUseRsD};  // Bit_Extender bit_extender_2
  not not_1 (not_1_out, comparator_1_eq);
  Comparator #(.width(5)) comparator_1 (.a({5{1'b0}}), .b(rsD), .eq(comparator_1_eq));  // open: gt, lt
  Comparator #(.width(5)) comparator_2 (.a(rsD), .b(EWA), .eq(comparator_2_eq));  // open: gt, lt
  Comparator #(.width(2), .mode("unsigned")) comparator_3 (
    .a(tNewE), .b(bit_extender_1_out), .gt(comparator_3_gt));  // open: eq, lt
  not not_2 (not_2_out, comparator_4_eq);
  Comparator #(.width(5)) comparator_4 (.a({5{1'b0}}), .b(rsD), .eq(comparator_4_eq));  // open: gt, lt
  Comparator #(.width(5)) comparator_5 (.a(rsD), .b(MWA), .eq(comparator_5_eq));  // open: gt, lt
  Comparator #(.width(2), .mode("unsigned")) comparator_6 (
    .a(tNewM), .b(bit_extender_2_out), .gt(comparator_6_gt));  // open: eq, lt
  Comparator #(.width(5)) comparator_7 (.a({5{1'b0}}), .b(rtD), .eq(comparator_7_eq));  // open: gt, lt
  not not_3 (not_3_out, comparator_7_eq);
  Comparator #(.width(5)) comparator_8 (.a(rtD), .b(EWA), .eq(comparator_8_eq));  // open: gt, lt
  Comparator #(.width(2), .mode("unsigned")) comparator_9 (
    .a(tNewE), .b(tUseRtD), .gt(comparator_9_gt));  // open: eq, lt
  not not_4 (not_4_out, comparator_10_eq);
  Comparator #(.width(5)) comparator_10 (.a({5{1'b0}}), .b(rtD), .eq(comparator_10_eq));  // open: gt, lt
  Comparator #(.width(5)) comparator_11 (.a(rtD), .b(MWA), .eq(comparator_11_eq));  // open: gt, lt
  Comparator #(.width(2), .mode("unsigned")) comparator_12 (
    .a(tNewM), .b(tUseRtD), .gt(comparator_12_gt));  // open: eq, lt
  and and_1 (and_1_out, not_1_out, comparator_2_eq, comparator_3_gt, tUseRsDEn, EwE);
  and and_2 (and_2_out, not_2_out, comparator_5_eq, comparator_6_gt, tUseRsDEn, MwE);
  and and_3 (and_3_out, not_3_out, comparator_8_eq, comparator_9_gt, tUseRtDEn, EwE);
  and and_4 (and_4_out, not_4_out, comparator_11_eq, comparator_12_gt, tUseRtDEn, MwE);
  or or_1 (stall, and_1_out, and_2_out, and_3_out, and_4_out);

  // Other names for the same wires on the sheet: tnE[1:0] = tNewE; tnM[1:0] = tNewM; tursD = tUseRsD;
  //   tursE = tUseRsDEn; turtD[1:0] = tUseRtD; turtE = tUseRtDEn
endmodule

module FWD (
  input  [31:0] rd,
  input  [4:0] ra,
  input  [31:0] d1,
  input  we1,
  input  [31:0] d2,
  input  [4:0] src1,
  input  we2,
  input  [4:0] src2,
  output [31:0] o
);

  wire comparator_1_eq, comparator_2_eq, comparator_3_eq, comparator_4_eq, not_1_out, not_2_out;
  wire [1:0] and_1_out;

  Comparator #(.width(5)) comparator_1 (.a(ra), .b({5{1'b0}}), .eq(comparator_1_eq));  // open: gt, lt
  Comparator #(.width(5)) comparator_2 (.a(ra), .b(src1), .eq(comparator_2_eq));  // open: gt, lt
  Comparator #(.width(5)) comparator_3 (.a(ra), .b({5{1'b0}}), .eq(comparator_3_eq));  // open: gt, lt
  Comparator #(.width(5)) comparator_4 (.a(ra), .b(src2), .eq(comparator_4_eq));  // open: gt, lt
  not not_1 (not_1_out, comparator_1_eq);
  not not_2 (not_2_out, comparator_3_eq);
  and and_1 (and_1_out[0], not_1_out, comparator_2_eq, we1);
  and and_2 (and_1_out[1], not_2_out, comparator_4_eq, we2);
  Multiplexer #(.select(2), .width(32)) multiplexer_1 (
    .in0(rd), .in1(d1), .in2(d2), .in3(d1), .out(o), .sel(and_1_out));  // open: en
endmodule
